# Fritzing sketch agam (saved by Fritzing 0.9.3b)

parts:
  CUI-enc1 = AMT103
  Part1 = Arduino Pro Mini v13
  M1 = DC Motor
  Part2 = Motor Driver 1A Dual TB6612FNG
  M2 = DC Motor
  Part3 = Arduino Pro Mini v13
  CUI-enc2 = AMT103
  Part7 = Arduino Mega 2560 (Rev3)
  Part8 = Arduino Pro Mini v13
  Part9 = Arduino Pro Mini v13
  CUI-enc3 = AMT103
  CUI-enc4 = AMT103
  M3 = DC Motor
  M4 = DC Motor
  Part11 = Motor Driver 1A Dual TB6612FNG

nets:
  N1: CUI-enc1.B, Part1.D3_PWM
  VCC: CUI-enc1.5V, Part1.VCC, Part2.VCC, Part3.VCC, CUI-enc2.5V
  N2: CUI-enc1.A, Part1.D2
  GND: CUI-enc1.GND, Part1.GND, Part2.GND, Part3.GND, CUI-enc2.GND
  N3: Part1.A4, Part3.A4, Part7.D20/SDA, Part8.A4, Part9.A4, Part9.A1
  N4: Part1.A5, Part3.A5, Part7.D21/SCL, Part8.A5, Part9.A5
  N5: Part1.D11_PWM/MOSI, Part2.PWMB
  N6: Part1.D10_PWM/SS, Part2.PWMA
  N7: Part1.D6_PWM, Part2.BIN2
  N8: Part1.D5_PWM, Part2.BIN1
  N9: M1.pin_1, Part2.A02
  N10: M1.pin_2, Part2.A01
  N11: Part2.B01, M2.pin_1
  N12: Part2.B02, M2.pin_2
  N13: Part2.AIN2, Part3.D6_PWM
  N14: Part2.AIN1, Part3.D5_PWM
  N15: Part3.D3_PWM, CUI-enc2.B
  N16: Part3.D2, CUI-enc2.A
  GND_2: Part8.GND, Part9.GND, CUI-enc3.GND, CUI-enc4.GND, Part11.GND
  VCC_2: Part8.VCC, Part9.VCC, CUI-enc3.5V, CUI-enc4.5V, Part11.VCC
  N17: Part8.D11_PWM/MOSI, Part11.PWMB
  N18: Part8.D10_PWM/SS, Part11.PWMA
  N19: Part8.D6_PWM, Part11.BIN2
  N20: Part8.D5_PWM, Part11.BIN1
  N21: Part8.D3_PWM, CUI-enc4.B
  N22: Part8.D2, CUI-enc4.A
  N23: Part9.D6_PWM, Part11.AIN2
  N24: Part9.D5_PWM, Part11.AIN1
  N25: Part9.D3_PWM, CUI-enc3.B
  N26: Part9.D2, CUI-enc3.A
  N27: M3.pin_1, Part11.B01
  N28: M3.pin_2, Part11.B02
  N29: M4.pin_1, Part11.A02
  N30: M4.pin_2, Part11.A01
